# Fritzing sketch ssd1306 (saved by Fritzing 0.9.6b)

parts:
  WeMos_D1_Mini1 = WeMos D1 Mini
  OLED2 = OLED 128x64 I2C Monochrome Display GND-VDD

nets:
  3V3: WeMos_D1_Mini1.3V3, OLED2.VDD
  N1: WeMos_D1_Mini1.D1, OLED2.SCK
  N2: WeMos_D1_Mini1.D2, OLED2.SDA
  N3: WeMos_D1_Mini1.G, OLED2.GND

custom parts:
  OLED 128x64 I2C Monochrome Display GND-VDD: OLED 128x64 I2C Monochrome Display. Note: there are two variants of this part, this one is the GND VDD SCK SDA variant. The other is VDD GND SCK SDA. Make sure you select the part that matches your module as using the incorrect part will probably destroy your module! In addition the mounting holes are marked on silkscreen but not by default drilled. If you want drilled mounting holes, copy a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
