# Fritzing sketch st7735 (saved by Fritzing 0.9.6b)

parts:
  WeMos_D1_Mini1 = WeMos D1 Mini
  LCD1 = 1_7in tft lcd

nets:
  N1: WeMos_D1_Mini1.3V3, LCD1.pin_8
  N2: WeMos_D1_Mini1.5V, LCD1.pin2
  N3: WeMos_D1_Mini1.D3, LCD1.pin_7
  N4: WeMos_D1_Mini1.D4, LCD1.pin_5
  N5: WeMos_D1_Mini1.D5, LCD1.pin3
  N6: WeMos_D1_Mini1.D7, LCD1.pin4
  N7: WeMos_D1_Mini1.D8, LCD1.pin_6
  N8: WeMos_D1_Mini1.G, LCD1.pin_1

custom parts:
  1_7in tft lcd: This is the Zoll 1.77in spi lcd display. The 1.77" display has 128x160 color pixels.
