# Fritzing sketch airmonitor (saved by Fritzing 0.9.6b)

parts:
  WeMos_D1_Mini1 = WeMos D1 Mini
  Mod1 = CJMCU-811
  OLED1 = OLED 128x64 I2C Monochrome Display
  J1 = SHT3X [form="♂ (male)" package=THT]

nets:
  3V3: WeMos_D1_Mini1.3V3, Mod1.VCC, OLED1.VDD, J1.VIN
  N1: WeMos_D1_Mini1.D1, Mod1.SDA, OLED1.SDA, J1.SDA/RH
  N2: WeMos_D1_Mini1.D2, Mod1.SCL, OLED1.SCK, J1.SCL/T
  GND: WeMos_D1_Mini1.G, Mod1.GND, Mod1.WAK, OLED1.GND, J1.GND

custom parts:
  CJMCU-811: The CCS811 is an ultra-low power digital gas sensor solution which integrates a metal oxide (MOX) gas sensor to detect a wide range of Volatile Organic Compounds (VOCs) for indoor air quality monitoring with a microcontroller unit (MCU), which includes an Analog-to-Digital converter (ADC), and an I²C interface.
  SHT3X: SHT31 SHT31-D Temperature & Humidity Sensor Breakout
