# Fritzing sketch crystallight (saved by Fritzing 0.9.6b)

parts:
  WeMos_D1_Mini1 = WeMos D1 Mini
  Bauteil1 = 16 NeoPixel Ring [part_number=1463]

nets:
  5V: WeMos_D1_Mini1.5V, Bauteil1.VDD
  N1: WeMos_D1_Mini1.D4, Bauteil1.IN
  N2: WeMos_D1_Mini1.G, Bauteil1.GND

custom parts:
  16 NeoPixel Ring: 16 ultra bright smart LED NeoPixels are arranged in a circle with 1.75" (44.5mm) outer diameter. The rings are 'chainable' - connect the output pin of one to the input pin of another. Use only one microcontroller pin to control as many as you can chain together! Each LED is addressable as the driver chip is inside the LED. Each one has ~18mA constant current drive so the color will be very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
