# Fritzing sketch bh1750 (saved by Fritzing 0.9.6b)

parts:
  WeMos_D1_Mini1 = WeMos D1 Mini
  Bauteil2 = BH1750

nets:
  3V3: WeMos_D1_Mini1.3V3, Bauteil2.VCC
  N1: WeMos_D1_Mini1.D1, Bauteil2.SCL
  N2: WeMos_D1_Mini1.D2, Bauteil2.SDA
  N3: WeMos_D1_Mini1.G, Bauteil2.GND

custom parts:
  BH1750: Light Sensor
