# Fritzing sketch bme280 (saved by Fritzing 0.9.6b)

parts:
  WeMos_D1_Mini1 = WeMos D1 Mini
  M1 = BME280

nets:
  3V3: WeMos_D1_Mini1.3V3, M1.VIN
  N1: WeMos_D1_Mini1.D1, M1.SCL
  N2: WeMos_D1_Mini1.D2, M1.SDA
  N3: WeMos_D1_Mini1.G, M1.GND

custom parts:
  BME280: Temperature Humidity Barometric presure Sensor
