# Fritzing sketch ccs811 (saved by Fritzing 0.9.6b)

parts:
  WeMos_D1_Mini1 = WeMos D1 Mini
  Mod1 = CJMCU-811

nets:
  3V3: WeMos_D1_Mini1.3V3, Mod1.VCC
  N1: WeMos_D1_Mini1.D1, Mod1.SCL
  N2: WeMos_D1_Mini1.D2, Mod1.SDA
  N3: WeMos_D1_Mini1.G, Mod1.GND, Mod1.WAK

custom parts:
  CJMCU-811: The CCS811 is an ultra-low power digital gas sensor solution which integrates a metal oxide (MOX) gas sensor to detect a wide range of Volatile Organic Compounds (VOCs) for indoor air quality monitoring with a microcontroller unit (MCU), which includes an Analog-to-Digital converter (ADC), and an I²C interface.
