# Fritzing sketch mpu6050 (saved by Fritzing 0.9.6b)

parts:
  WeMos_D1_Mini1 = WeMos D1 Mini
  Bauteil1 = InvenSense MPU6050

nets:
  3V3: WeMos_D1_Mini1.3V3, Bauteil1.VCC
  N1: WeMos_D1_Mini1.D1, Bauteil1.SCL
  N2: WeMos_D1_Mini1.D2, Bauteil1.SDA
  N3: WeMos_D1_Mini1.G, Bauteil1.GND
