# Fritzing sketch QMC5883L (saved by Fritzing 0.9.6b)

parts:
  WeMos_D1_Mini1 = WeMos D1 Mini
  Module1 = Boladge HMC5883L Compass Module

nets:
  3V3: WeMos_D1_Mini1.3V3, Module1.VCC
  N1: WeMos_D1_Mini1.D1, Module1.SCL
  N2: WeMos_D1_Mini1.D2, Module1.SDA
  N3: WeMos_D1_Mini1.G, Module1.GND

custom parts:
  Boladge HMC5883L Compass Module: Cheap digital compass module
