# Fritzing sketch sht30 (saved by Fritzing 0.9.6b)

parts:
  WeMos_D1_Mini1 = WeMos D1 Mini
  J1 = SHT3X [form="♂ (male)" package=THT]

nets:
  3V3: WeMos_D1_Mini1.3V3, J1.VIN
  N1: WeMos_D1_Mini1.D1, J1.SCL/T
  N2: WeMos_D1_Mini1.D2, J1.SDA/RH
  N3: WeMos_D1_Mini1.G, J1.GND

custom parts:
  SHT3X: SHT31 SHT31-D Temperature & Humidity Sensor Breakout
