# Fritzing sketch vl53l0x (saved by Fritzing 0.9.6b)

parts:
  WeMos_D1_Mini1 = WeMos D1 Mini
  Bauteil2 = GY-VL53L0XV2 Laser Ranger Module

nets:
  3V3: WeMos_D1_Mini1.3V3, Bauteil2.VCC
  N1: WeMos_D1_Mini1.D1, Bauteil2.SCL
  N2: WeMos_D1_Mini1.D2, Bauteil2.SDA
  N3: WeMos_D1_Mini1.G, Bauteil2.GND

custom parts:
  GY-VL53L0XV2 Laser Ranger Module: The GY-VL53L0XV2 is based on the VL53L0X from ST Microelectronics, a time-of-flight ranging system integrated into a compact module.
